// Logisim project memorias.circ as structural Verilog: 10 circuits, main circuit Ram 1x2
module Ram_1x2 (
  input  Clock,
  input  [1:0] Entrada,
  input  Enable,
  input  Clear,
  output [1:0] Output
);

  wire not_1_out, not_2_out;

  not not_1 (not_1_out, Entrada[0]);
  not not_2 (not_2_out, Entrada[1]);
  J_K_Flip_Flop j_k_ff_1 (
    .J(Entrada[0]), .clk(Clock), .K(not_1_out), .Q(Output[0]), .en(Enable), .reset(Clear));  // open: Qn, preset
  J_K_Flip_Flop j_k_ff_2 (
    .J(Entrada[1]), .clk(Clock), .K(not_2_out), .Q(Output[1]), .en(Enable), .reset(Clear));  // open: Qn, preset
endmodule

module Ram_1x4 (
  input  clock,
  input  [3:0] entrada,
  input  enable,
  input  Clear,
  output [3:0] \output 
);

  wire [1:0] ram_1x2_1_output, ram_1x2_2_output;

  Ram_1x2 ram_1x2_1 (.Entrada(entrada[1:0]), .Clock(clock), .Enable(enable), .Clear(Clear), .Output(ram_1x2_1_output));
  Ram_1x2 ram_1x2_2 (.Entrada(entrada[3:2]), .Clock(clock), .Enable(enable), .Clear(Clear), .Output(ram_1x2_2_output));
  and and_1 (\output [0], enable, ram_1x2_1_output[0]);
  and and_2 (\output [1], enable, ram_1x2_1_output[1]);
  and and_3 (\output [2], enable, ram_1x2_2_output[0]);
  and and_4 (\output [3], enable, ram_1x2_2_output[1]);
endmodule

module Ram_2x4 (
  input  Clock,
  input  [3:0] in,
  input  [1:0] \endereço ,
  input  clear,
  output [3:0] \output 
);

  wire \endereço_2x4_1__0 , \endereço_2x4_1__1 , \endereço_2x4_1__2 , \endereço_2x4_1__3 ;
  wire [3:0] ram_1x4_1_output, ram_1x4_2_output, ram_1x4_3_output, ram_1x4_4_output;

  \Endereço_2x4  \endereço_2x4_1  (
    .Entrada(\endereço ), ._0(\endereço_2x4_1__0 ), ._1(\endereço_2x4_1__1 ), ._2(\endereço_2x4_1__2 ),
    ._3(\endereço_2x4_1__3 ));
  Ram_1x4 ram_1x4_1 (
    .entrada(in), .clock(Clock), .enable(\endereço_2x4_1__0 ), .Clear(clear), .\output (ram_1x4_1_output));
  Ram_1x4 ram_1x4_2 (
    .entrada(in), .clock(Clock), .enable(\endereço_2x4_1__1 ), .Clear(clear), .\output (ram_1x4_2_output));
  Ram_1x4 ram_1x4_3 (
    .entrada(in), .clock(Clock), .enable(\endereço_2x4_1__2 ), .Clear(clear), .\output (ram_1x4_3_output));
  Ram_1x4 ram_1x4_4 (
    .entrada(in), .clock(Clock), .enable(\endereço_2x4_1__3 ), .Clear(clear), .\output (ram_1x4_4_output));
  assign \output  = ram_1x4_1_output | ram_1x4_2_output | ram_1x4_3_output | ram_1x4_4_output;  // OR_Gate or_1, 4 bits wide
endmodule

module \Endereço_2x4  (
  input  [1:0] Entrada,
  output _0,
  output _1,
  output _2,
  output _3
);

  wire not_1_out, not_2_out, not_3_out, not_4_out;

  not not_1 (not_1_out, Entrada[0]);
  and and_1 (_0, not_1_out, not_2_out);
  not not_2 (not_2_out, Entrada[1]);
  not not_3 (not_3_out, Entrada[0]);
  and and_2 (_1, not_3_out, Entrada[1]);
  and and_3 (_2, Entrada[0], not_4_out);
  not not_4 (not_4_out, Entrada[1]);
  and and_4 (_3, Entrada[0], Entrada[1]);
endmodule

module Ram_1x8 (
  input  clo,
  input  [7:0] in,
  input  en,
  input  cle,
  output [7:0] out
);

  Ram_1x4 ram_1x4_1 (.entrada(in[3:0]), .clock(clo), .enable(en), .Clear(cle), .\output (out[3:0]));
  Ram_1x4 ram_1x4_2 (.entrada(in[7:4]), .clock(clo), .enable(en), .Clear(cle), .\output (out[7:4]));
endmodule

module RAM_2x8 (
  input  in_1,
  input  [7:0] in_2,
  input  in_3,
  input  in_4,
  output [7:0] out_5
);

  wire \endereço_1x2_1__0 , \endereço_1x2_1__1 ;
  wire [7:0] ram_1x8_1_out, ram_1x8_2_out;

  \Endereço_1x2  \endereço_1x2_1  (.in(in_3), ._0(\endereço_1x2_1__0 ), ._1(\endereço_1x2_1__1 ));
  Ram_1x8 ram_1x8_1 (.in(in_2), .clo(in_1), .en(\endereço_1x2_1__0 ), .cle(in_4), .out(ram_1x8_1_out));
  Ram_1x8 ram_1x8_2 (.in(in_2), .clo(in_1), .en(\endereço_1x2_1__1 ), .cle(in_4), .out(ram_1x8_2_out));
  assign out_5 = ram_1x8_1_out | ram_1x8_2_out;  // OR_Gate or_1, 8 bits wide
endmodule

module \Endereço_1x2  (
  input  in,
  output _0,
  output _1
);

  not not_1 (_0, in);

  assign _1 = in;
endmodule

module Ram_4x8 (
  input  clock,
  input  [3:0] in,
  input  [1:0] \endereço ,
  input  clear,
  output [3:0] out
);

  wire \endereço_2x4_1__0 , \endereço_2x4_1__1 , \endereço_2x4_1__2 , \endereço_2x4_1__3 ;
  wire [3:0] ram_2x4_1_p5, ram_2x4_2_p5, ram_2x4_3_p5, ram_2x4_4_p5;

  \Endereço_2x4  \endereço_2x4_1  (
    .Entrada(\endereço ), ._0(\endereço_2x4_1__0 ), ._1(\endereço_2x4_1__1 ), ._2(\endereço_2x4_1__2 ),
    ._3(\endereço_2x4_1__3 ));
  // Ram_2x4 ram_2x4_1: pin names not known; wires that end beside it: in, clock, \endereço_2x4_1__0 , clear, ram_2x4_1_p5
  // Ram_2x4 ram_2x4_2: pin names not known; wires that end beside it: in, clock, \endereço_2x4_1__1 , clear, ram_2x4_2_p5
  // Ram_2x4 ram_2x4_3: pin names not known; wires that end beside it: in, clock, \endereço_2x4_1__2 , clear, ram_2x4_3_p5
  // Ram_2x4 ram_2x4_4: pin names not known; wires that end beside it: in, clock, \endereço_2x4_1__3 , clear, ram_2x4_4_p5
  assign out = ram_2x4_1_p5 | ram_2x4_3_p5 | ram_2x4_4_p5 | ram_2x4_2_p5;  // OR_Gate or_1, 4 bits wide
endmodule

module \Endereço_3x8  (
  input  [2:0] in,
  output _0,
  output _1,
  output _2,
  output _3,
  output _4,
  output _5,
  output _6,
  output _7
);

  wire not_1_out, not_2_out, not_3_out, not_4_out, not_5_out, not_6_out, not_7_out, not_8_out, not_9_out,
       not_10_out, not_11_out, not_12_out;

  not not_1 (not_1_out, in[2]);
  not not_2 (not_2_out, in[1]);
  not not_3 (not_3_out, in[0]);
  not not_4 (not_4_out, in[2]);
  not not_5 (not_5_out, in[1]);
  not not_6 (not_6_out, in[2]);
  not not_7 (not_7_out, in[0]);
  not not_8 (not_8_out, in[2]);
  not not_9 (not_9_out, in[1]);
  not not_10 (not_10_out, in[0]);
  not not_11 (not_11_out, in[1]);
  not not_12 (not_12_out, in[0]);
  and and_1 (_0, not_1_out, not_2_out, not_3_out);
  and and_2 (_1, not_4_out, not_5_out, in[0]);
  and and_3 (_2, not_6_out, in[1], not_7_out);
  and and_4 (_3, not_8_out, in[1], in[0]);
  and and_5 (_4, in[2], not_9_out, not_10_out);
  and and_6 (_5, in[2], not_11_out, in[0]);
  and and_7 (_6, in[2], in[1], not_12_out);
  and and_8 (_7, in[2], in[1], in[0]);
endmodule

module Ram_8x8 (
  input  in_1,
  input  [7:0] in_2,
  input  [2:0] in_3,
  input  in_4,
  output [7:0] out_5
);

  wire \endereço_3x8_1__0 , \endereço_3x8_1__1 , \endereço_3x8_1__2 , \endereço_3x8_1__3 ,
       \endereço_3x8_1__4 , \endereço_3x8_1__5 , \endereço_3x8_1__6 , \endereço_3x8_1__7 ;
  wire [7:0] ram_1x8_1_out, ram_1x8_2_out, ram_1x8_3_out, ram_1x8_4_out, ram_1x8_5_out, ram_1x8_6_out,
       ram_1x8_7_out, ram_1x8_8_out;

  \Endereço_3x8  \endereço_3x8_1  (
    .in(in_3), ._0(\endereço_3x8_1__0 ), ._1(\endereço_3x8_1__1 ), ._2(\endereço_3x8_1__2 ),
    ._3(\endereço_3x8_1__3 ), ._4(\endereço_3x8_1__4 ), ._5(\endereço_3x8_1__5 ), ._6(\endereço_3x8_1__6 ),
    ._7(\endereço_3x8_1__7 ));
  Ram_1x8 ram_1x8_1 (.in(in_2), .clo(in_1), .en(\endereço_3x8_1__0 ), .cle(in_4), .out(ram_1x8_1_out));
  Ram_1x8 ram_1x8_2 (.in(in_2), .clo(in_1), .en(\endereço_3x8_1__1 ), .cle(in_4), .out(ram_1x8_2_out));
  Ram_1x8 ram_1x8_3 (.in(in_2), .clo(in_1), .en(\endereço_3x8_1__2 ), .cle(in_4), .out(ram_1x8_3_out));
  Ram_1x8 ram_1x8_4 (.in(in_2), .clo(in_1), .en(\endereço_3x8_1__3 ), .cle(in_4), .out(ram_1x8_4_out));
  Ram_1x8 ram_1x8_5 (.in(in_2), .clo(in_1), .en(\endereço_3x8_1__4 ), .cle(in_4), .out(ram_1x8_5_out));
  Ram_1x8 ram_1x8_6 (.in(in_2), .clo(in_1), .en(\endereço_3x8_1__5 ), .cle(in_4), .out(ram_1x8_6_out));
  Ram_1x8 ram_1x8_7 (.in(in_2), .clo(in_1), .en(\endereço_3x8_1__6 ), .cle(in_4), .out(ram_1x8_7_out));
  Ram_1x8 ram_1x8_8 (.in(in_2), .clo(in_1), .en(\endereço_3x8_1__7 ), .cle(in_4), .out(ram_1x8_8_out));
  assign out_5 = ram_1x8_1_out | ram_1x8_2_out | ram_1x8_5_out | ram_1x8_6_out | ram_1x8_7_out | ram_1x8_8_out | ram_1x8_3_out | ram_1x8_4_out;  // OR_Gate or_1, 8 bits wide
endmodule
