// Logisim project Movimentacao_De_Dados.circ as structural Verilog: 5 circuits, main circuit Movimento de bit para a direita
module Movimento_de_bit_para_a_direita (
  input  clock,
  input  data,
  input  clear,
  output a,
  output b,
  output c,
  output d,
  output e,
  output a_2
);

  D_Flip_Flop d_ff_1 (.clk(clock), .D(data), .Q(a), .reset(clear));  // open: Qn, preset, en
  D_Flip_Flop d_ff_2 (.clk(clock), .D(a), .Q(b), .reset(clear));  // open: Qn, preset, en
  D_Flip_Flop d_ff_3 (.clk(clock), .D(b), .Q(c), .reset(clear));  // open: Qn, preset, en
  D_Flip_Flop d_ff_4 (.clk(clock), .D(c), .Q(d), .reset(clear));  // open: Qn, preset, en
  D_Flip_Flop d_ff_5 (.clk(clock), .D(d), .Q(e), .reset(clear));  // open: Qn, preset, en
  D_Flip_Flop d_ff_6 (.clk(clock), .D(e), .Q(a_2), .reset(clear));  // open: Qn, preset, en
endmodule

module Movimento_de_bit_para_a_esquerda (
  input  clock,
  input  data,
  input  clear,
  output a,
  output b,
  output c,
  output d,
  output e,
  output e_2
);

  D_Flip_Flop d_ff_1 (.clk(clock), .D(b), .Q(a), .reset(clear));  // open: Qn, preset, en
  D_Flip_Flop d_ff_2 (.clk(clock), .D(c), .Q(b), .reset(clear));  // open: Qn, preset, en
  D_Flip_Flop d_ff_3 (.clk(clock), .D(d), .Q(c), .reset(clear));  // open: Qn, preset, en
  D_Flip_Flop d_ff_4 (.clk(clock), .D(e), .Q(d), .reset(clear));  // open: Qn, preset, en
  D_Flip_Flop d_ff_5 (.clk(clock), .D(e_2), .Q(e), .reset(clear));  // open: Qn, preset, en
  D_Flip_Flop d_ff_6 (.clk(clock), .D(data), .Q(e_2), .reset(clear));  // open: Qn, preset, en
endmodule

module Ring_Direita (
  input  clock,
  input  data,
  input  clear,
  output out_4,
  output out_5,
  output out_6,
  output out_7,
  output out_8,
  output out_9
);

  wire or_1_out;

  or or_1 (or_1_out, out_9, data);
  D_Flip_Flop d_ff_1 (.clk(clock), .D(or_1_out), .Q(out_4), .reset(clear));  // open: Qn, preset, en
  D_Flip_Flop d_ff_2 (.clk(clock), .D(out_4), .Q(out_5), .reset(clear));  // open: Qn, preset, en
  D_Flip_Flop d_ff_3 (.clk(clock), .D(out_5), .Q(out_6), .reset(clear));  // open: Qn, preset, en
  D_Flip_Flop d_ff_4 (.clk(clock), .D(out_6), .Q(out_7), .reset(clear));  // open: Qn, preset, en
  D_Flip_Flop d_ff_5 (.clk(clock), .D(out_7), .Q(out_8), .reset(clear));  // open: Qn, preset, en
  D_Flip_Flop d_ff_6 (.clk(clock), .D(out_8), .Q(out_9), .reset(clear));  // open: Qn, preset, en
endmodule

module Twisted_ring_Esquerda (
  input  in_1,
  input  in_2,
  input  in_3,
  output out_4,
  output out_5,
  output out_6,
  output out_7,
  output out_8,
  output out_9
);

  wire d_ff_1_qn, or_1_out;

  D_Flip_Flop d_ff_1 (.clk(in_1), .D(out_5), .Q(out_4), .Qn(d_ff_1_qn), .reset(in_3));  // open: preset, en
  D_Flip_Flop d_ff_2 (.clk(in_1), .D(out_6), .Q(out_5), .reset(in_3));  // open: Qn, preset, en
  D_Flip_Flop d_ff_3 (.clk(in_1), .D(out_7), .Q(out_6), .reset(in_3));  // open: Qn, preset, en
  D_Flip_Flop d_ff_4 (.clk(in_1), .D(out_8), .Q(out_7), .reset(in_3));  // open: Qn, preset, en
  D_Flip_Flop d_ff_5 (.clk(in_1), .D(out_9), .Q(out_8), .reset(in_3));  // open: Qn, preset, en
  or or_1 (or_1_out, d_ff_1_qn, in_2);
  D_Flip_Flop d_ff_6 (.clk(in_1), .D(or_1_out), .Q(out_9), .reset(in_3));  // open: Qn, preset, en
endmodule

module Serial_Paralelo (
  input  in_1,
  input  in_2,
  input  in_3,
  input  in_4,
  input  in_5,
  input  in_6,
  input  in_7,
  input  in_8,
  input  in_9,
  output out_10,
  output out_11,
  output out_12,
  output out_13,
  output out_14,
  output out_15
);

  wire and_1_out, and_2_out, and_3_out, and_4_out, and_5_out, and_6_out;

  and and_1 (and_1_out, in_4, in_3);
  D_Flip_Flop d_ff_1 (.clk(in_1), .D(1'b0), .Q(out_10), .preset(and_1_out), .reset(in_2));  // open: Qn, en
  D_Flip_Flop d_ff_2 (.clk(in_1), .D(out_10), .Q(out_11), .preset(and_2_out), .reset(in_2));  // open: Qn, en
  and and_2 (and_2_out, in_5, in_3);
  D_Flip_Flop d_ff_3 (.clk(in_1), .D(out_11), .Q(out_12), .preset(and_3_out), .reset(in_2));  // open: Qn, en
  and and_3 (and_3_out, in_6, in_3);
  and and_4 (and_4_out, in_7, in_3);
  D_Flip_Flop d_ff_4 (.clk(in_1), .D(out_12), .Q(out_13), .preset(and_4_out), .reset(in_2));  // open: Qn, en
  and and_5 (and_5_out, in_8, in_3);
  D_Flip_Flop d_ff_5 (.clk(in_1), .D(out_13), .Q(out_14), .preset(and_5_out), .reset(in_2));  // open: Qn, en
  D_Flip_Flop d_ff_6 (.clk(in_1), .D(out_14), .Q(out_15), .preset(and_6_out), .reset(in_2));  // open: Qn, en
  and and_6 (and_6_out, in_9, in_3);
endmodule
